# Fritzing sketch conexiones (saved by Fritzing 0.9.3b)
breadboards: 1

parts:
  Raspberry_Pi_Zero1 = Raspberry Pi Zero
  J1 = Basic Servo
  J2 = Basic Servo
  M2 = DC Motor
  Componente1 = Power Cell LiPo Charger/Booster
  Componente2 = PowerBoost 500 Charger  # not connected
  VCC1 = Battery
  V1 = DC Power [voltage=5]  # not connected
  Pololu_A1 = Pololu A4988 [package=SO16]
  M1 = DC Motor
  U1 = SWITCH_SPDT [package=kps-1290]
  J3 = Basic Servo
  U2 = TRANSCHIPTC5747 [package=camera_sfv24r-2st_2]
  D1 = Rectifier Diode [package="Melf DO-213 AA [SMD]"]
  C1 = Capacitor Polarized [package=cpol-radial-100uf-25v]

nets:
  GND: Raspberry_Pi_Zero1.GND, J1.gnd, J2.gnd, Pololu_A1.MS3, J3.gnd, C1.-
  N1: Raspberry_Pi_Zero1.GPIO17, Pololu_A1.MS1
  N2: Raspberry_Pi_Zero1.GPIO22, Pololu_A1.STEP
  N3: Raspberry_Pi_Zero1.GPIO10, J3.pulse
  N4: Raspberry_Pi_Zero1.GPIO9, J2.pulse
  N5: Raspberry_Pi_Zero1.GPIO11, J1.pulse
  N6: Raspberry_Pi_Zero1.GPIO23, Pololu_A1.SLEEP
  N7: Raspberry_Pi_Zero1.GPIO18, Pololu_A1.MS2
  N8: Raspberry_Pi_Zero1.5V, D1.cathode, C1.+
  VCC: J1.vcc, J2.vcc, Pololu_A1.RESET, J3.vcc
  N9: M2.pin_1, Pololu_A1.1A
  N10: M2.pin_2, Pololu_A1.1B
  N11: Componente1.VCC, U1.O
  N12: VCC1.+, U1.P
  N13: Pololu_A1.2A, M1.pin_2
  N14: Pololu_A1.2B, M1.pin_1
  N15: U1.S, D1.anode
  N16: U2.SCLK, U2.AGND, U2.AVDD28, U2.RESET_N
  N17: U2.DOUT_0, U2.DOUT_1, U2.DOUT_2, U2.DOUT_3, U2.DOUT_4
  N18: U2.DOUT_7, U2.DOUT_8, U2.VCLK_OUT, U2.VALIDH, U2.VALIDV
  N19: U2.PS1, U2.PS2, U2.SHIELD, U2.LED_CTRL

notes:
  2x18650 en Paralelo
  Booster 3.7v-7v
  TP4056 Cargador
  DRV8833
  Servos dirección y pasajeros
  PiCamera
  100uF
